// Logisim project wk6ex1-4.circ as structural Verilog: 7 circuits, main circuit MyXOR
module MyXOR (
);


  // Notes on the sheet:
  //   Hier kan je een XOR-schakeling bouwen
  //   Je kan de tutorial volgen (in het Help-menu; "tutorial") of zelf de oplossing bedenken...
endmodule

module FullAdder (
  input  X,
  input  Y,
  input  CarryIn,
  output Sum,
  output CarryOut
);

  wire not_1_out;

  not not_1 (not_1_out, X);

  // Notes on the sheet:
  //   3 invoerbits:  X,  Y en CarryIn
  //   Hier kan je een FULL-ADDERschakeling bouwen
  //   (1) teken de andere vier rails   (2) je hebt 8 AND-poorten nodig    (3)  je hebt twee OR-poorten nodig
  //   twee uitvoerbits:  Sum en CarryOut
endmodule

module Een_4bit_Ripple_Carry_Adder (
  input  Y3,
  input  Y2,
  input  Y1,
  input  Y0,
  input  X3,
  input  X2,
  input  X1,
  input  X0,
  output Sum4,
  output Sum3,
  output Sum2,
  output Sum1,
  output Sum0
);


  // Notes on the sheet:
  //   Hier kan je een 4-bit-RIPPLE-CARRY-ADDERschakeling bouwen
  //   8 invoerbits
  //   5 uitvoerbits
endmodule

module Een_4bit_vermenigvuldiger (
  input  Y3,
  input  Y2,
  input  Y1,
  input  Y0,
  input  X3,
  input  X2,
  input  X1,
  input  X0,
  output Z7,
  output Z6,
  output Z5,
  output Z4,
  output Z3,
  output Z2,
  output Z1,
  output Z0
);


  // Notes on the sheet:
  //   factor (4 bits)
  //   See the problem for details on this hint:   Build a 4x1-bit multiplier first!
  //   tweede factor (4 bits)
  //   product (8 bits)
  //   4-bit-VERMENIGVULDIGINGSschakeling
  //   meest significante (hoogste) uitvoerbit
  //   minst significante (laagste) uitvoerbit
endmodule

module Een_3bij2_deler (
  input  Y2,
  input  Y1,
  input  Y0,
  input  X1,
  input  X0,
  output Z2,
  output Z1,
  output Z0,
  output Error
);


  // Notes on the sheet:
  //   Teller (3 bits: Y2 Y1 Y0)
  //   Noemer (2 bits: X1 X0)
  //   Quotiënt (4 bits: Z2 Z1 Z0 en Error)
  //   3-bij-2-bit-DELINGSschakeling
endmodule

module Een_2bit_decoder (
);


  // Notes on the sheet:
  //   2-bit-DECODERschakeling (bonusopgave)
endmodule

module Een_12nGb_geheugen (
);


  // Notes on the sheet:
  //   12-nanogigabit-GEHEUGENschakelin (bonusopgave)
endmodule
